# Fritzing sketch Synthesizer_Clock_Module_Fritzing_Files (saved by Fritzing 0.9.10b)
circuit board: 8.46667cm x 5.64444cm
breadboards: 1

parts:
  MCU_Arduino_Nano = Arduino Nano (Rev3.0)
  ENCODER1 = KY-040
  JRC4558 = Dual Op-Amp [package=dip08]
  Tempo_Button_1 = Square Pushbutton
  D1 = Diode [package=diode-1n4148]
  Signal_out1 = female pin header, 2 pins [form="♀ (female)"]
  R1 = Resistor [tolerance=±5% power=0.25 resistance=100000 package=THT]
  12V_Input = female pin header, 2 pins [form="♀ (female)"]
  R2 = Resistor [tolerance=±5% power=0.25 resistance=100000 package=THT]
  Signal_out2 = female pin header, 2 pins [form="♀ (female)"]
  VIN = female pin header, 2 pins [form="♀ (female)"]
  D2 = Diode [package=diode-1n4148]
  64_x_32_OLED_I2C = Grove 3 Axis Digital Accelerometer 16g

nets:
  GND: MCU_Arduino_Nano.GND, ENCODER1.GND, Tempo_Button_1.leg0, VIN.pin2, 64_x_32_OLED_I2C.GND
  N1: MCU_Arduino_Nano.D3, Tempo_Button_1.leg1
  N2: MCU_Arduino_Nano.D4, ENCODER1.SW
  N3: MCU_Arduino_Nano.D5, ENCODER1.DT
  N4: MCU_Arduino_Nano.D6, ENCODER1.CLK
  N5: MCU_Arduino_Nano.D12/MISO, D2.A
  N6: MCU_Arduino_Nano.VIN, VIN.pin1
  N7: MCU_Arduino_Nano.A5, 64_x_32_OLED_I2C.SCL
  N8: MCU_Arduino_Nano.A4, 64_x_32_OLED_I2C.SDA
  3V3: MCU_Arduino_Nano.3V3, ENCODER1.+, 64_x_32_OLED_I2C.VCC
  N9: MCU_Arduino_Nano.D13/SCK, D1.A
  N10: JRC4558.A_OUT, JRC4558.A_-IN, Signal_out1.pin1, Signal_out1.pin2
  N11: JRC4558.A_+IN, D1.C, R1.Pin_0
  N12: JRC4558.A_V-, R1.Pin_1, 12V_Input.pin2, R2.Pin_1
  N13: JRC4558.B_+IN, R2.Pin_0, D2.C
  N14: JRC4558.B_-IN, JRC4558.B_OUT, Signal_out2.pin1, Signal_out2.pin2
  N15: JRC4558.A_V+, 12V_Input.pin1

notes:
  JRC4558 seems to work, but the signal is inverted. Would be nice to find a circuit or part that can not be inverted from the input and output between 3V low and 12V high
  Synth Sequencer Clock Module, The goal of this circuit is to provide some clock signal through an arduino.  , 1.0.0
  Vcc
  GND

custom parts:
  KY-040: Rotary encoder with button
